# Fritzing sketch 01 (saved by Fritzing 0.7.12b)
breadboards: 1

parts:
  Arduino1 = Arduino
  LED1 = LED - 5mm [color="Red (633nm)" package="5 mm [THT]"]
  LCD1 = LCD screen  # not connected
  J2 = Basic Servo
  J3 = Basic Servo
  R1 = 470 Ω Resistor [package=THT]
  J4 = Infrared Proximity Sensor
  J5 = Infrared Proximity Sensor
  LED2 = green smd LED [package="1206 [SMD]"]
  R2 = 470 Ω Resistor [package=THT]

nets:
  N1: Arduino1.D13, R2.Pin_1
  N2: Arduino1.D12, R1.Pin_1
  N3: Arduino1.D9, J3.pulse
  N4: Arduino1.D8, J2.pulse
  VCC: Arduino1.+5V, J2.vcc, J3.vcc, J4.Vcc, J5.Vcc
  GND: Arduino1.GND, LED1.cathode, J2.gnd, J3.gnd, J4.GND, J5.GND, LED2.cathode
  N5: Arduino1.A1, J5.Vout
  N6: LED1.anode, R1.Pin_0
  N7: LED2.anode, R2.Pin_0
